# Fritzing sketch arduboy_fritz (saved by Fritzing 0.9.10b)
breadboards: 2

parts:
  Part4 = OLED Monochrome 128x64 1.3 inch [part_number=938]
  S8 = Pushbutton [package="[THT]"]
  S9 = Pushbutton [package="[THT]"]
  S10 = Pushbutton [package="[THT]"]
  S11 = Pushbutton [package="[THT]"]
  S12 = Pushbutton [package="[THT]"]
  S13 = Pushbutton [package="[THT]"]
  S14 = Pushbutton [package="[THT]"]
  Part5 = Arduino Pro Micro (Clone)
  J1 = Piezo Speaker

nets:
  GND: Part4.MOSI_SDA, Part4.GND, S8.Pin_3, S8.Pin_4, S9.Pin_3, S9.Pin_4, S10.Pin_3, S10.Pin_4, S11.Pin_3, S11.Pin_4, S12.Pin_3, S12.Pin_4, S13.Pin_3, S13.Pin_4, S14.Pin_3, S14.Pin_4, Part5.GND, J1.pin1
  N1: Part4.SCLK_SCK, Part5.VCC
  N2: Part4.DC_SA0, Part5.D15
  N3: Part4.RESET, Part5.D16
  N4: Part4.CS, Part5.D6
  N5: Part4.VIN, Part5.D4
  N6: S8.Pin_1, S8.Pin_2, Part5.A2
  N7: S9.Pin_1, S9.Pin_2, Part5.A1
  N8: S10.Pin_1, S10.Pin_2, Part5.RST
  N9: S11.Pin_1, S11.Pin_2, Part5.A0
  N10: S12.Pin_1, S12.Pin_2, Part5.D8
  N11: S13.Pin_1, S13.Pin_2, Part5.D7
  N12: S14.Pin_1, S14.Pin_2, Part5.A3
  N13: Part5.D5, J1.pin2

custom parts:
  OLED Monochrome 128x64 1.3 inch: These displays are small, only about 1.3" diagonal, but very readable due to the high contrast of an OLED display. This display is made of 128x64 individual white OLED pixels, each one is turned on or off by the controller chip. Because the display makes its own light, no backlight is required. This reduces the power required to run the OLED and is why the display has such high contrast; we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
